# Fritzing sketch PI-HC-SR04 (saved by Fritzing 0.9.3b)
breadboards: 1

parts:
  Raspberry_Pi_1 = Raspberry Pi 3 [part_number=RPI-3-V1.2]
  R1 = Resistor [tolerance=±5% resistance=680 package=THT]
  R2 = Resistor [tolerance=±5% resistance=470 package=THT]

nets:
  N1: Raspberry_Pi_1.GIPO21, R1.Pin_1, R2.Pin_1
  N2: Raspberry_Pi_1.GND, R1.Pin_0
